# Fritzing sketch ArduinoBatteryMonitor (saved by Fritzing 0.7.5b)
perfboards: 1

parts:
  + = Screw terminal - 2 pins [package=THT]
  R1 = Resistor [tolerance=±5% resistance=33k package=THT]
  D1 = Rectifier Diode [part_number=1N4001 package="300 mil [THT]"]
  R2 = Resistor [tolerance=±5% resistance=100k package=THT]
  Arduino1 = Arduino

nets:
  N1: +.pin1, R1.Pin_1, Arduino1.GND
  N2: +.pin2, D1.anode
  N3: R1.Pin_0, R2.Pin_1
  N4: D1.cathode, R2.Pin_0, Arduino1.VIN
